# Fritzing sketch gps_tracker (saved by Fritzing 0.9.3b)
breadboards: 1

parts:
  Part1 = MicroSD Card Module
  Part2 = Arduino Nano (Rev3.0)
  LCM1602_IIC1 = LCM1602 IIC [part_number="LCM1602 IIC" chip_label="LCM1602 IIC" package="DIP (Dual Inline) [THT]"]
  U1 = LCD-16X2 [package=lcd-16x2]

nets:
  GND: Part1.GND, Part2.GND, LCM1602_IIC1.GND
  VCC: Part1.VCC, Part2.5V, LCM1602_IIC1.VCC
  N1: Part1.MISO, Part2.D12/MISO
  N2: Part1.MOSI, Part2.D11/MOSI
  N3: Part1.SCK, Part2.D4
  N4: Part1.CS, Part2.D13/SCK
  N5: Part2.A5, LCM1602_IIC1.SCL
  N6: Part2.A4, LCM1602_IIC1.SDA
  VSS: LCM1602_IIC1.VSS, U1.VSS
  VDD: LCM1602_IIC1.VDD, U1.VDD
  N7: LCM1602_IIC1.V0, U1.VO
  N8: LCM1602_IIC1.RS, U1.RS
  N9: LCM1602_IIC1.RW, U1.R_W
  N10: LCM1602_IIC1.E, U1.E
  N11: LCM1602_IIC1.D0, U1.DB0
  N12: LCM1602_IIC1.D1, U1.DB1
  N13: LCM1602_IIC1.D2, U1.DB2
  N14: LCM1602_IIC1.D3, U1.DB3
  N15: LCM1602_IIC1.D4, U1.DB4
  N16: LCM1602_IIC1.D5, U1.DB5
  N17: LCM1602_IIC1.D6, U1.DB6
  N18: LCM1602_IIC1.D7, U1.DB7
  N19: LCM1602_IIC1.A, U1.A
  N20: LCM1602_IIC1.K, U1.K
  N21: LCM1602_IIC1.LED_A, LCM1602_IIC1.LED_B

notes:
  [Connect GPS module]
  blue - GND
  white - TX
  green - RX
  red - VCC

custom parts:
  LCM1602 IIC: I2C-Module to use a 1602 or 2004 LCD on with the wire.h libory Serial LCD Modul
